// Logisim project ADD_1.circ as structural Verilog: 2 circuits, main circuit main
module main (
  input  in_1,
  input  in_2,
  input  in_3,
  output out_4,
  output out_5
);

  ADD_1 add_1_1 (.S(out_5), .Vai_1(out_4), .a(in_1), .b(in_2), .Vem_1(in_3));
endmodule

module ADD_1 (
  input  a,
  input  b,
  input  Vem_1,
  output S,
  output Vai_1
);

  wire and_1_out, and_2_out, or_1_out, xor_1_out;

  and and_1 (and_1_out, b, Vem_1);
  xor xor_1 (xor_1_out, b, a);
  or or_1 (or_1_out, Vem_1, b);
  xor xor_2 (S, Vem_1, xor_1_out);
  and and_2 (and_2_out, or_1_out, a);
  or or_2 (Vai_1, and_2_out, and_1_out);
endmodule
