// Logisim project ADD_2.circ as structural Verilog: 3 circuits, main circuit main
module main (
  input  [3:0] in_1,
  input  [3:0] in_2,
  output out_3,
  output [3:0] out_4
);

  // Probe on in_1
  // Probe on in_2
  ADD_4 add_4_1 (.A(in_1), .Overflow(out_3), .B(in_2), .S(out_4));
  // Probe on out_4
endmodule

module ADD_1 (
  input  a,
  input  b,
  input  Vem_1,
  output S,
  output Vai_1
);

  wire and_1_out, and_2_out, or_1_out, xor_1_out;

  and and_1 (and_1_out, b, Vem_1);
  xor xor_1 (xor_1_out, b, a);
  or or_1 (or_1_out, Vem_1, b);
  xor xor_2 (S, Vem_1, xor_1_out);
  and and_2 (and_2_out, or_1_out, a);
  or or_2 (Vai_1, and_2_out, and_1_out);
endmodule

module ADD_4 (
  input  [3:0] B,
  input  [3:0] A,
  output Overflow,
  output [3:0] S
);

  wire add_1_2_vai_1, add_1_3_vai_1, add_1_4_vai_1;

  // Probe on A
  ADD_1 add_1_1 (.S(S[3]), .Vai_1(Overflow), .a(A[3]), .b(B[3]), .Vem_1(add_1_2_vai_1));
  ADD_1 add_1_2 (.S(S[2]), .Vai_1(add_1_2_vai_1), .a(A[2]), .b(B[2]), .Vem_1(add_1_3_vai_1));
  ADD_1 add_1_3 (.S(S[1]), .Vai_1(add_1_3_vai_1), .a(A[1]), .b(B[1]), .Vem_1(add_1_4_vai_1));
  // Probe on S
  ADD_1 add_1_4 (.S(S[0]), .Vai_1(add_1_4_vai_1), .a(A[0]), .b(B[0]), .Vem_1(1'b0));
  // Probe on B
endmodule
