// Logisim project EXE_1.circ as structural Verilog: 2 circuits, main circuit main
module main (
  input  in_1,
  input  in_2,
  input  in_3,
  output out_4
);

  EXE_1 exe_1_1 (.out_4(out_4), .A(in_1), .B(in_2), .C(in_3));
endmodule

module EXE_1 (
  input  A,
  input  B,
  input  C,
  output out_4
);

  wire and_1_out, or_1_out, xor_1_out;

  and and_1 (and_1_out, or_1_out, ~A);  // AND_Gate
  xor xor_1 (xor_1_out, B, A);
  or or_1 (or_1_out, ~B, xor_1_out);  // OR_Gate
  or or_2 (out_4, and_1_out, ~C);  // OR_Gate
endmodule
